// Logisim project B2_Group01.circ as structural Verilog: 3 circuits, main circuit main
module main (
  input  in_1,
  output [15:0] out_2,
  output [7:0] PC,
  output [3:0] zero,
  output [3:0] t0,
  output [3:0] t1,
  output [3:0] t2,
  output [3:0] t3,
  output [3:0] t4,
  output [3:0] sp
);

  wire and_1_out, Clock_out, controlwithrom_1_alusrc, controlwithrom_1_bne, controlwithrom_1_branch,
       controlwithrom_1_jump, controlwithrom_1_memread, controlwithrom_1_memtoreg, controlwithrom_1_memwrite,
       controlwithrom_1_regdst, controlwithrom_1_regwrite, controlwithrom_1_shiftcontrol,
       controlwithrom_1_shiftleftorright, n74181_1_p10, or_1_out, xor_1_out;
  wire [3:0] multiplexer_1_out, multiplexer_2_out, multiplexer_5_out, multiplexer_6_out, multiplexer_7_out,
       multiplexer_8_out, n74181_1_p7, ram_1_data, register_file_v2_1_read01, register_file_v2_1_read02,
       shifter_1_out, shifter_2_out;
  wire [5:0] controlwithrom_1_alu_op;
  wire [7:0] adder_1_out, adder_2_out, bit_extender_1_out, multiplexer_3_out, multiplexer_4_out;

  Register To_Store_PC (.D(multiplexer_4_out), .Q(PC), .clk(Clock_out), .clr(in_1));  // open: en
  Adder adder_1 (.a(8'h1), .b(PC), .out(adder_1_out));  // open: cin, cout
  assign bit_extender_1_out = {{4{out_2[3]}}, out_2[3:0]};  // Bit_Extender bit_extender_1
  ROM #(.dataWidth(16)) rom_1 (.addr(PC), .data(out_2));  // open: sel
  Multiplexer #(.width(4), .enable("false")) multiplexer_1 (
    .in0(out_2[7:4]), .in1(out_2[3:0]), .out(multiplexer_1_out), .sel(controlwithrom_1_regdst));
  Clock Clock (.out(Clock_out));
  Adder adder_2 (.a(adder_1_out), .b(bit_extender_1_out), .out(adder_2_out));  // open: cin, cout
  controlWithRom controlwithrom_1 (
    .Opcode(out_2[15:12]), .Alu_Op(controlwithrom_1_alu_op), .RegDst(controlwithrom_1_regdst),
    .Jump(controlwithrom_1_jump), .Branch(controlwithrom_1_branch), .BNE(controlwithrom_1_bne),
    .MemRead(controlwithrom_1_memread), .MemtoReg(controlwithrom_1_memtoreg),
    .MemWrite(controlwithrom_1_memwrite), .AluSrc(controlwithrom_1_alusrc),
    .RegWrite(controlwithrom_1_regwrite), .ShiftControl(controlwithrom_1_shiftcontrol),
    .ShiftLeftOrRight(controlwithrom_1_shiftleftorright));
  register_file_v2 register_file_v2_1 (
    .ReadRegister01(out_2[11:8]), .ReadRegister02(out_2[7:4]), .WriteRegister(multiplexer_1_out),
    .Clk(Clock_out), .RegWrite(controlwithrom_1_regwrite), .DataToBeWritten(multiplexer_7_out),
    .sw_1_lw_0(controlwithrom_1_memwrite), .Read01(register_file_v2_1_read01),
    .Read02(register_file_v2_1_read02), .zero(zero), .t0(t0), .t1(t1), .t2(t2), .t3(t3), .t4(t4), .sp(sp));
  Multiplexer #(.width(4), .enable("false")) multiplexer_2 (
    .in0(register_file_v2_1_read02), .in1(out_2[3:0]), .out(multiplexer_2_out), .sel(controlwithrom_1_alusrc));
  // _74181 74181_1: pin names not known; wires that end beside it: controlwithrom_1_alu_op[3], controlwithrom_1_alu_op[2], controlwithrom_1_alu_op[1], controlwithrom_1_alu_op[0], controlwithrom_1_alu_op[4], controlwithrom_1_alu_op[5], n74181_1_p7, register_file_v2_1_read01, multiplexer_2_out, n74181_1_p10
  and and_1 (and_1_out, controlwithrom_1_branch, xor_1_out);
  xor xor_1 (xor_1_out, controlwithrom_1_bne, n74181_1_p10);
  Multiplexer #(.width(8), .enable("false")) multiplexer_3 (
    .in0(adder_1_out), .in1(adder_2_out), .out(multiplexer_3_out), .sel(and_1_out));
  RAM #(.addrWidth(4), .dataWidth(4), .bus("separate")) ram_1 (
    .addr(n74181_1_p7), .din(register_file_v2_1_read02), .data(ram_1_data), .str(controlwithrom_1_memwrite),
    .clk(Clock_out), .ld(controlwithrom_1_memread), .clr(in_1));  // open: sel
  Shifter #(.width(4)) shifter_1 (.in(register_file_v2_1_read01), .\dist (out_2[1:0]), .out(shifter_1_out));
  Shifter #(.width(4), .shift("lr")) shifter_2 (
    .in(register_file_v2_1_read01), .\dist (out_2[1:0]), .out(shifter_2_out));
  or or_1 (or_1_out, out_2[2], out_2[3]);
  Multiplexer #(.width(8), .enable("false")) multiplexer_4 (
    .in0(multiplexer_3_out), .in1(out_2[11:4]), .out(multiplexer_4_out), .sel(controlwithrom_1_jump));
  Multiplexer #(.width(4), .enable("false")) multiplexer_5 (
    .in0(n74181_1_p7), .in1(ram_1_data), .out(multiplexer_5_out), .sel(controlwithrom_1_memtoreg));
  Multiplexer #(.width(4), .enable("false")) multiplexer_6 (
    .in0(shifter_1_out), .in1(shifter_2_out), .out(multiplexer_6_out), .sel(controlwithrom_1_shiftleftorright));
  Multiplexer #(.width(4), .enable("false")) multiplexer_7 (
    .in0(multiplexer_5_out), .in1(multiplexer_8_out), .out(multiplexer_7_out),
    .sel(controlwithrom_1_shiftcontrol));
  Multiplexer #(.width(4), .enable("false")) multiplexer_8 (
    .in0(multiplexer_6_out), .in1(4'b0000), .out(multiplexer_8_out), .sel(or_1_out));

  // Notes on the sheet:
  //   contents of rom_1 (hex, n*v repeats v):
  //   5023 203e 8231 d234 b135 6323 f331 3341 4190 e441 334 506f 6620 663f 4180 7131 f552 c531 e551 a225
  //   63f c324 630 4190 1128
endmodule

module register_file_v2 (
  input  [3:0] ReadRegister01,
  input  [3:0] ReadRegister02,
  input  [3:0] WriteRegister,
  input  Clk,
  input  RegWrite,
  input  [3:0] DataToBeWritten,
  input  sw_1_lw_0,
  output [3:0] Read01,
  output [3:0] Read02,
  output [3:0] zero,
  output [3:0] t0,
  output [3:0] t1,
  output [3:0] t2,
  output [3:0] t3,
  output [3:0] t4,
  output [3:0] sp
);

  wire and_1_out, decoder_1_out1, decoder_1_out2, decoder_1_out3, decoder_1_out4, decoder_1_out5,
       decoder_1_out6, not_1_out;
  wire [3:0] adder_1_out, adder_2_out, multiplexer_1_out, multiplexer_2_out;

  not not_1 (not_1_out, ReadRegister01[0]);
  Decoder #(.select(3), .disabled(0)) decoder_1 (
    .out1(decoder_1_out1), .out2(decoder_1_out2), .out3(decoder_1_out3), .out4(decoder_1_out4),
    .out5(decoder_1_out5), .out6(decoder_1_out6), .sel(WriteRegister[2:0]), .en(RegWrite));  // open: out0, out7
  and and_1 (and_1_out, not_1_out, ReadRegister01[1], ReadRegister01[2]);
  Register #(.width(4)) u_t0 (.D(DataToBeWritten), .en(decoder_1_out1), .Q(t0), .clk(Clk));  // open: clr
  Register #(.width(4)) u_t1 (.D(DataToBeWritten), .en(decoder_1_out2), .Q(t1), .clk(Clk));  // open: clr
  Register #(.width(4)) u_t2 (.D(DataToBeWritten), .en(decoder_1_out3), .Q(t2), .clk(Clk));  // open: clr
  Register #(.width(4)) u_t3 (.D(DataToBeWritten), .en(decoder_1_out4), .Q(t3), .clk(Clk));  // open: clr
  Register #(.width(4)) u_t4 (.D(DataToBeWritten), .en(decoder_1_out5), .Q(t4), .clk(Clk));  // open: clr
  Register #(.width(4), .trigger("falling")) u_sp (
    .D(multiplexer_2_out), .en(and_1_out), .Q(sp), .clk(Clk));  // open: clr
  Adder #(.width(4)) adder_1 (.a(sp), .b(4'b1111), .out(adder_1_out));  // open: cin, cout
  Multiplexer #(.width(4), .disabled(0), .enable("false")) multiplexer_1 (
    .in0(sp), .in1(adder_1_out), .out(multiplexer_1_out), .sel(sw_1_lw_0));
  Adder #(.width(4)) adder_2 (.a(sp), .b(4'b0001), .out(adder_2_out));  // open: cin, cout
  Multiplexer #(.width(4), .disabled(0), .enable("false")) multiplexer_2 (
    .in0(adder_2_out), .in1(adder_1_out), .out(multiplexer_2_out), .sel(sw_1_lw_0));
  Multiplexer #(.select(3), .width(4), .disabled(0), .enable("false")) multiplexer_3 (
    .in0(4'b0000), .in1(t0), .in2(t1), .in3(t2), .in4(t3), .in5(t4), .in6(multiplexer_1_out), .out(Read01),
    .sel(ReadRegister01[2:0]));  // open: in7
  Multiplexer #(.select(3), .width(4), .disabled(0), .enable("false")) multiplexer_4 (
    .in0(4'b0000), .in1(t0), .in2(t1), .in3(t2), .in4(t3), .in5(t4), .in6(multiplexer_1_out), .out(Read02),
    .sel(ReadRegister02[2:0]));  // open: in7

  assign zero = 4'b0000;
endmodule

module controlWithRom (
  input  [3:0] Opcode,
  output [5:0] Alu_Op,
  output RegDst,
  output Jump,
  output Branch,
  output BNE,
  output MemRead,
  output MemtoReg,
  output MemWrite,
  output AluSrc,
  output RegWrite,
  output ShiftControl,
  output ShiftLeftOrRight
);

  ROM #(.addrWidth(4), .dataWidth(17)) rom_1 (
    .addr(Opcode),
    .data({ShiftLeftOrRight, ShiftControl, RegWrite, AluSrc, MemWrite, MemtoReg, MemRead, BNE, Branch, Jump, RegDst, Alu_Op}));  // open: sel

  // Notes on the sheet:
  //   contents of rom_1 (hex, n*v repeats v):
  //   6c19 306 6006 106 80 6019 3019 406e 4059 406b 602e 4061 602b 4046 c000 1c000
endmodule
