// Logisim project control.circ as structural Verilog: 1 circuit, main circuit main
module main (
  input  a,
  input  b,
  input  c,
  input  d,
  output w,
  output x,
  output y,
  output z,
  output c_2,
  output m
);

  wire and_1_out, and_2_out, and_3_out, and_4_out, and_5_out, and_6_out, and_7_out, and_8_out, and_9_out,
       and_10_out, and_11_out, and_12_out, and_13_out, and_14_out, and_15_out, and_16_out, and_17_out,
       and_18_out, and_19_out, and_20_out, and_21_out, and_22_out, and_23_out, not_1_out, not_2_out,
       not_3_out, not_4_out, not_5_out, not_6_out, not_7_out, not_8_out, not_9_out, not_10_out, not_11_out,
       not_12_out, not_13_out, not_14_out, not_15_out, not_16_out, not_17_out, not_18_out, not_19_out,
       not_20_out, not_21_out, not_22_out, not_23_out, not_24_out, not_25_out, not_26_out, not_27_out,
       not_28_out, not_29_out;

  not not_1 (not_1_out, c);
  and and_1 (and_1_out, not_1_out, not_2_out);
  not not_2 (not_2_out, d);
  not not_3 (not_3_out, a);
  and and_2 (and_2_out, not_3_out, b);
  and and_3 (and_3_out, a, not_4_out, not_5_out);
  not not_4 (not_4_out, b);
  not not_5 (not_5_out, c);
  and and_4 (and_4_out, a, not_6_out);
  not not_6 (not_6_out, d);
  not not_7 (not_7_out, a);
  and and_5 (and_5_out, not_7_out, not_8_out, d);
  not not_8 (not_8_out, b);
  not not_9 (not_9_out, b);
  and and_6 (and_6_out, not_9_out, c, not_10_out);
  not not_10 (not_10_out, d);
  not not_11 (not_11_out, a);
  and and_7 (and_7_out, not_11_out, c, d);
  and and_8 (and_8_out, a, b, d);
  not not_12 (not_12_out, b);
  and and_9 (and_9_out, not_12_out, not_13_out, d);
  not not_13 (not_13_out, c);
  not not_14 (not_14_out, a);
  and and_10 (and_10_out, not_14_out, not_15_out, c);
  not not_15 (not_15_out, b);
  not not_16 (not_16_out, b);
  and and_11 (and_11_out, not_16_out, c, not_17_out);
  not not_17 (not_17_out, d);
  not not_18 (not_18_out, a);
  and and_12 (and_12_out, not_18_out, c, d);
  and and_13 (and_13_out, a, b);
  not not_19 (not_19_out, c);
  and and_14 (and_14_out, not_19_out, not_20_out);
  not not_20 (not_20_out, d);
  not not_21 (not_21_out, a);
  and and_15 (and_15_out, not_21_out, b, not_22_out);
  not not_22 (not_22_out, c);
  and and_16 (and_16_out, b, not_23_out);
  not not_23 (not_23_out, d);
  and and_17 (and_17_out, a, not_24_out, d);
  not not_24 (not_24_out, b);
  not not_25 (not_25_out, c);
  and and_18 (and_18_out, not_25_out, not_26_out);
  not not_26 (not_26_out, d);
  not not_27 (not_27_out, a);
  and and_19 (and_19_out, not_27_out, b);
  and and_20 (and_20_out, b, c, d);
  not not_28 (not_28_out, b);
  and and_21 (and_21_out, a, not_28_out, d);
  and and_22 (and_22_out, a, c);
  and and_23 (and_23_out, a, b, not_29_out);
  not not_29 (not_29_out, d);
  or or_1 (w, and_1_out, and_2_out, and_3_out, and_4_out);
  or or_2 (x, and_5_out, and_6_out, and_7_out, and_8_out);
  or or_3 (y, and_9_out, and_10_out, and_11_out, and_12_out, and_13_out);
  or or_4 (z, and_14_out, and_15_out, and_16_out, and_17_out);
  or or_5 (c_2, and_18_out, and_19_out);
  or or_6 (m, and_20_out, and_21_out, and_22_out, and_23_out);
endmodule
